// Logisim project LogisimGodinezJoseph.circ as structural Verilog
module NotGate (
  input  in_1,
  output out_2
);

  not not_1 (out_2, in_1);

  // Notes on the sheet:
  //   Not Gate
endmodule

module ANDGate2input (
  input  in_1,
  input  in_2,
  output out_3
);

  and and_1 (out_3, in_1, in_2);

  // Notes on the sheet:
  //   AND Gate with 2 inputs
endmodule

module ANDGate3input (
  input  in_1,
  input  in_2,
  input  in_3,
  output out_4
);

  and and_1 (out_4, in_1, in_2, in_3);

  // Notes on the sheet:
  //   AND Gate with 3 inputs
endmodule

module ORGate2input (
  input  in_1,
  input  in_2,
  output out_3
);

  or or_1 (out_3, in_1, in_2);

  // Notes on the sheet:
  //   OR Gate with 2 input
endmodule

module ORGate3input (
  input  in_1,
  input  in_2,
  input  in_3,
  output out_4
);

  or or_1 (out_4, in_1, in_2, in_3);

  // Notes on the sheet:
  //   OR Gate with 3 inputs
endmodule

module NANDGate2input (
  input  in_1,
  input  in_2,
  output out_3
);

  nand nand_1 (out_3, in_1, in_2);

  // Notes on the sheet:
  //   NAND Gate with 2 inputs
endmodule

module NORGate2input (
  input  in_1,
  input  in_2,
  output out_3
);

  nor nor_1 (out_3, in_1, in_2);

  // Notes on the sheet:
  //   NOR Gate with 2 inputs
endmodule

module XORGate2input (
  input  in_1,
  input  in_2,
  output out_3
);

  xor xor_1 (out_3, in_1, in_2);

  // Notes on the sheet:
  //   XOR Gate with 2 inputs
endmodule

module Decoder2input4output (
  input  in_1,
  input  in_2,
  output out_3,
  output out_4,
  output out_5,
  output out_6
);

  and and_1 (out_3, ~in_1, ~in_2);  // AND_Gate
  and and_2 (out_4, ~in_1, in_2);  // AND_Gate
  and and_3 (out_5, in_1, ~in_2);  // AND_Gate
  and and_4 (out_6, in_1, in_2);

  // Notes on the sheet:
  //   Decoder with 2 inputs and 4 outputs
endmodule

module MUX2to1 (
  input  in_1,
  input  in_2,
  input  in_3,
  output out_4
);

  wire and_1_out, and_2_out;

  and and_1 (and_1_out, in_1, in_3);
  or or_1 (out_4, and_1_out, and_2_out);
  and and_2 (and_2_out, in_2, in_3);

  // Notes on the sheet:
  //   A 2-to-1 Multiplexer
endmodule

module MUX4t (
  input  in_1,
  input  in_2,
  input  in_3,
  input  in_4,
  input  in_5,
  input  in_6,
  output out_7
);

  wire and_1_out, and_2_out, and_3_out, and_4_out;

  and and_1 (and_1_out, in_1, ~in_6, ~in_5);  // AND_Gate
  and and_2 (and_2_out, in_2, ~in_6, in_5);  // AND_Gate
  or or_1 (out_7, and_1_out, and_2_out, and_3_out, and_4_out);
  and and_3 (and_3_out, in_3, in_6, ~in_5);  // AND_Gate
  and and_4 (and_4_out, in_4, in_6, in_5);

  // Notes on the sheet:
  //   4 Input MUX
endmodule

module RSlatch (
  input  in_1,
  input  in_2,
  output out_3,
  output out_4
);

  nand nand_1 (out_3, in_1, out_4);
  nand nand_2 (out_4, out_3, in_2);

  // Notes on the sheet:
  //   R-S Latch with R-S input
endmodule

module DGated (
  input  in_1,
  input  in_2,
  output out_3,
  output out_4
);

  wire nand_1_out, nand_2_out;

  nand nand_1 (nand_1_out, in_1, in_2);
  nand nand_2 (nand_2_out, in_2, ~in_1);  // NAND_Gate
  nand nand_3 (out_3, nand_1_out, out_4);
  nand nand_4 (out_4, out_3, nand_2_out);

  // Notes on the sheet:
  //   Gated D
endmodule

module onebitAdder (
  input  in_1,
  input  in_2,
  input  in_3,
  output out_4,
  output out_5
);

  wire and_1_out, and_2_out, and_3_out, and_4_out, and_5_out, and_6_out, and_7_out, and_8_out;

  and and_1 (and_1_out, ~in_1, ~in_2, ~in_3);  // AND_Gate
  and and_2 (and_2_out, ~in_1, ~in_2, in_3);  // AND_Gate
  and and_3 (and_3_out, ~in_1, in_2, ~in_3);  // AND_Gate
  and and_4 (and_4_out, ~in_1, in_2, in_3);  // AND_Gate
  and and_5 (and_5_out, in_1, ~in_2, ~in_3);  // AND_Gate
  and and_6 (and_6_out, in_1, ~in_2, in_3);  // AND_Gate
  and and_7 (and_7_out, in_1, in_2, ~in_3);  // AND_Gate
  and and_8 (and_8_out, in_1, in_2, in_3);
  or or_1 (out_4, and_4_out, and_6_out, and_7_out, and_8_out);
  or or_2 (out_5, and_8_out, and_2_out, and_3_out, and_5_out);

  // Notes on the sheet:
  //   One bit Adder
endmodule

module two4bitadder (
  input  A0,
  input  B2,
  input  B1,
  input  C2,
  input  B3,
  input  A3,
  input  in_7,
  input  B0,
  input  _0,
  output C3,
  output C1,
  output out_12,
  output C4,
  output S1,
  output S3,
  output out_16,
  output S2
);

  onebitAdder onebitadder_1 (.in_1(A0), .in_2(B0), .in_3(_0), .out_4(C1), .out_5(out_16));
  onebitAdder onebitadder_2 (.in_1(B1), .in_2(in_7), .in_3(C1), .out_4(out_12), .out_5(S1));
  onebitAdder onebitadder_3 (.in_1(B2), .in_2(C2), .in_3(out_12), .out_4(C3), .out_5(S2));
  onebitAdder onebitadder_4 (.in_1(A3), .in_2(B3), .in_3(C3), .out_4(C4), .out_5(S3));

  // Notes on the sheet:
  //   S0
  //   A1
  //   two 4-bit adder
  //   A2
endmodule
