// Logisim project LogisimLabCircuit.circ as structural Verilog
module onebitadder (
  input  in_1,
  input  in_2,
  input  in_3,
  output out_4,
  output out_5
);

  wire and_1_out, and_2_out, and_3_out, and_4_out, and_5_out, and_6_out, and_7_out, and_8_out;

  and and_1 (and_1_out, ~in_1, ~in_2, ~in_3);  // AND_Gate
  and and_2 (and_2_out, ~in_1, ~in_2, in_3);  // AND_Gate
  and and_3 (and_3_out, ~in_1, in_2, ~in_3);  // AND_Gate
  and and_4 (and_4_out, ~in_1, in_2, in_3);  // AND_Gate
  and and_5 (and_5_out, in_1, ~in_2, ~in_3);  // AND_Gate
  and and_6 (and_6_out, in_1, ~in_2, in_3);  // AND_Gate
  and and_7 (and_7_out, in_1, in_2, ~in_3);  // AND_Gate
  and and_8 (and_8_out, in_1, in_2, in_3);
  or or_1 (out_4, and_4_out, and_6_out, and_7_out, and_8_out);
  or or_2 (out_5, and_8_out, and_2_out, and_3_out, and_5_out);
endmodule

module fourbitadder (
  input  A0,
  input  B2,
  input  B1,
  input  in_4,
  input  B3,
  input  A3,
  input  in_7,
  input  B0,
  input  _0,
  output C4,
  output S1,
  output S3,
  output out_13,
  output S2
);

  wire onebitadder_1_out_4, onebitadder_2_out_4, onebitadder_3_out_4;

  onebitadder onebitadder_1 (.in_1(A0), .in_2(B0), .in_3(_0), .out_4(onebitadder_1_out_4), .out_5(out_13));
  onebitadder onebitadder_2 (
    .in_1(B1), .in_2(in_7), .in_3(onebitadder_1_out_4), .out_4(onebitadder_2_out_4), .out_5(S1));
  onebitadder onebitadder_3 (
    .in_1(B2), .in_2(in_4), .in_3(onebitadder_2_out_4), .out_4(onebitadder_3_out_4), .out_5(S2));
  onebitadder onebitadder_4 (.in_1(A3), .in_2(B3), .in_3(onebitadder_3_out_4), .out_4(C4), .out_5(S3));

  // Notes on the sheet:
  //   S0
  //   A1
  //   A2
endmodule

module eightbitadder (
  input  [7:0] in_1,
  input  in_2,
  input  [7:0] in_3,
  output out_4,
  output [7:0] out_5
);

  wire fourbitadder_1_c4;

  fourbitadder fourbitadder_1 (
    .S1(out_5[1]), .in_7(in_1[1]), .B1(in_3[1]), .B2(in_3[2]), .A3(in_3[3]), .C4(fourbitadder_1_c4),
    .B0(in_3[0]), .in_4(in_1[2]), .A0(in_1[0]), .B3(in_1[3]), ._0(in_2), .S3(out_5[3]), .out_13(out_5[0]),
    .S2(out_5[2]));
  fourbitadder fourbitadder_2 (
    .S1(out_5[5]), .in_7(in_1[5]), .B1(in_3[5]), .B2(in_3[6]), .A3(in_3[7]), .C4(out_4), .B0(in_3[4]),
    .in_4(in_1[6]), .A0(in_1[4]), .B3(in_1[7]), ._0(fourbitadder_1_c4), .S3(out_5[7]), .out_13(out_5[4]),
    .S2(out_5[6]));
endmodule

module sixteenbitadder (
  input  [15:0] in_1,
  input  [15:0] in_2,
  input  in_3,
  output out_4,
  output [15:0] out_5
);

  wire eightbitadder_1_out_4;

  eightbitadder eightbitadder_1 (
    .out_5(out_5[7:0]), .in_1(in_1[7:0]), .out_4(eightbitadder_1_out_4), .in_2(in_3), .in_3(in_2[7:0]));
  eightbitadder eightbitadder_2 (
    .out_5(out_5[15:8]), .in_1(in_1[15:8]), .out_4(out_4), .in_2(eightbitadder_1_out_4), .in_3(in_2[15:8]));
endmodule

module eightbitregister (
  input  [7:0] in_1,
  input  in_2,
  input  in_3,
  output [7:0] out_4
);

  Register register_1 (.D(in_1), .en(in_2), .clk(in_3), .Q(out_4));  // open: clr
  DotMatrix #(.inputtype("row"), .matrixcols(8), .matrixrows(1)) dotmatrix_1 (.row0(out_4));
endmodule
